# Fritzing sketch car (saved by Fritzing 0.9.3b)
circuit board: 11.3395cm x 5.81953cm
breadboards: 1

parts:
  HC-SR04_Sensor_1 = HC-SR04 Ultrasonic Distance Sensor [part_number=2]
  HC-SR04_Sensor_2 = HC-SR04 Ultrasonic Distance Sensor [part_number=1]
  HC-SR04_Sensor_3 = HC-SR04 Ultrasonic Distance Sensor [part_number=3]
  LED1 = LED - 5mm [color="Red (633nm)" package="5 mm [THT]"]
  LED2 = LED - 5mm [color="Yellow (585nm)" package="5 mm [THT]"]
  LED3 = LED - 5mm [color="Green (555nm)" package="5 mm [THT]"]
  U1 = ESP8266 WiFi Module [part_number=ESP8266]
  JP1 = Header 4 [part_number=2 package=1x04-smd]
  JP2 = Header 4 [part_number=1 package=1x04-smd]
  JP3 = Header 4 [part_number=3 package=1x04-smd]
  Part1 = Arduino Uno (Rev3)

nets:
  VCC: HC-SR04_Sensor_1.VCC, HC-SR04_Sensor_2.VCC, HC-SR04_Sensor_3.VCC, JP1.1, JP2.1, JP3.1, Part1.5V
  N1: HC-SR04_Sensor_1.TRIG, HC-SR04_Sensor_2.TRIG, HC-SR04_Sensor_3.TRIG, JP1.2, JP2.2, JP3.2, Part1.D2
  N2: HC-SR04_Sensor_1.ECHO, JP1.3, Part1.D3_PWM
  GND: HC-SR04_Sensor_1.GND, HC-SR04_Sensor_2.GND, HC-SR04_Sensor_3.GND, LED1.cathode, LED2.cathode, LED3.cathode, U1.GND, JP1.4, JP2.4, JP3.4, Part1.GND
  N3: HC-SR04_Sensor_2.ECHO, JP2.3, Part1.D4
  N4: HC-SR04_Sensor_3.ECHO, JP3.3, Part1.D5_PWM
  N5: LED1.anode, Part1.A0
  N6: LED2.anode, Part1.A1
  N7: LED3.anode, Part1.A2
  VCC_2: U1.VCC, Part1.3V3
  N8: U1.TXD, Part1.D1/TX
